// Logisim project fourBitAdder.circ as structural Verilog: 2 circuits, main circuit main
module main (
  input  C_in,
  input  [3:0] A,
  input  [3:0] B,
  output [3:0] Sum,
  output C_out
);

  wire onebitadder_1_c_out, onebitadder_2_c_out, onebitadder_3_c_out;

  OneBitAdder onebitadder_1 (.A(A[0]), .B(B[0]), .C_in(C_in), .D(Sum[0]), .C_out(onebitadder_1_c_out));
  OneBitAdder onebitadder_2 (.A(A[1]), .B(B[1]), .C_in(onebitadder_1_c_out), .D(Sum[1]), .C_out(onebitadder_2_c_out));
  OneBitAdder onebitadder_3 (.A(A[2]), .B(B[2]), .C_in(onebitadder_2_c_out), .D(Sum[2]), .C_out(onebitadder_3_c_out));
  OneBitAdder onebitadder_4 (.A(A[3]), .B(B[3]), .C_in(onebitadder_3_c_out), .D(Sum[3]), .C_out(C_out));
endmodule

module OneBitAdder (
  input  A,
  input  B,
  input  C_in,
  output D,
  output C_out
);

  wire and_1_out, and_2_out, and_3_out, xor_1_out;

  xor xor_1 (xor_1_out, A, B);
  and and_1 (and_1_out, A, B);
  and and_2 (and_2_out, A, C_in);
  and and_3 (and_3_out, B, C_in);
  xor xor_2 (D, xor_1_out, C_in);
  or or_1 (C_out, and_1_out, and_2_out, and_3_out);
endmodule
