// Logisim project oneBitAdd.circ as structural Verilog: 1 circuit, main circuit main
module main (
  input  A,
  input  B,
  input  C_in,
  output D,
  output C_out
);

  wire and_1_out, and_3_out, xor_1_out;

  xor xor_1 (xor_1_out, A, B);
  // AND_Gate and_1 has open pins: out=and_1_out
  // AND_Gate and_2 has open pins: out=and_1_out
  // AND_Gate and_3 has open pins: out=and_3_out
  // XOR_Gate xor_2 has open pins: out=D
  or or_1 (C_out, and_1_out, and_1_out);
endmodule
